# Fritzing sketch Circuito Avionica 1 (saved by Fritzing 0.9.3b)
breadboards: 1

parts:
  Componente1 = Arduino Nano (Rev3.0)
  Componente2 = MicroSD Card Module
  Componente4 = LSM303C (6 DOF)  # not connected
  U2 = RELAY [package=relay-jzc]
  VCC2 = Battery block 9V
  S1 = Square Pushbutton
  Componente5 = LilyPad LED
  SG1 = Buzzer 12mm [package=buzzer-12mm]
  VCC4 = Battery block 9V

nets:
  N1: Componente1.D6, SG1.1
  N2: Componente1.D8, U2.COIL2
  N3: Componente1.D10, Componente2.GND
  N4: Componente1.D11/MOSI, Componente2.MISO
  N5: Componente1.D12/MISO, Componente2.MOSI
  N6: Componente1.VIN, S1.leg0
  N7: Componente1.D13/SCK, Componente2.VCC
  N8: Componente2.CS, U2.NC, VCC2.-, SG1.2
  N9: U2.MAIN, VCC4.+
  N10: U2.COIL1, Componente5.+
  N11: Componente5.-, VCC4.-

notes:
  e-match
