# Fritzing sketch Circuito Avionica 2 (saved by Fritzing 0.9.3b)
breadboards: 1

parts:
  Componente1 = Arduino Nano (Rev3.0)
  Componente2 = MicroSD Card Module
  Componente4 = LSM303C (6 DOF)  # not connected
  VCC1 = Battery block 9V
  U2 = RELAY [package=relay-jzc]
  SG2 = Buzzer 12mm [package=buzzer-12mm-ns-kit]  # not connected
  S1 = SWITCH-MOMENTARY-2 [package=tactile_switch_smd-2]  # not connected
  S2 = Round Pushbutton  # not connected
  VCC2 = Battery block 9V

nets:
  N1: Componente1.GND, VCC1.-
  N2: Componente1.D8, U2.COIL2
  N3: Componente1.D12/MISO, Componente2.MISO
  N4: Componente1.5V, VCC1.+, U2.NO
  N5: Componente1.D13/SCK, Componente2.SCK
  N6: U2.COIL1, VCC2.+
