# Fritzing sketch Circuito Avionica (saved by Fritzing 0.9.3b)
breadboards: 1

parts:
  Componente1 = Arduino Nano (Rev3.0)
  Componente2 = MicroSD Card Module
  Componente4 = LSM303C (6 DOF)  # not connected
  VCC1 = Battery block 9V
  U2 = RELAY [package=relay-jzc]
  VCC2 = Battery block 9V
  VCC3 = Battery block 9V
  S1 = Square Pushbutton
  Componente5 = LilyPad LED
  SG1 = Buzzer 12mm [package=buzzer-12mm]

nets:
  N1: Componente1.GND, VCC1.-, U2.NC, SG1.1
  N2: Componente1.D6, SG1.2
  N3: Componente1.D8, U2.NO
  N4: Componente1.D12/MISO, Componente2.MISO
  N5: Componente1.VIN, S1.leg1
  N6: Componente1.5V, U2.COIL2
  N7: Componente1.D13/SCK, Componente2.SCK
  N8: VCC1.+, S1.leg0
  N9: U2.MAIN, Componente5.+
  N10: U2.COIL1, VCC2.+, VCC3.+
  N11: VCC2.-, VCC3.-, Componente5.-

notes:
  e-match
